// Logisim project 4_bit_MUX.circ as structural Verilog: 1 circuit, main circuit main
module main (
  input  [3:0] number_a,
  input  [3:0] number_b,
  input  [3:0] in_3,
  input  [3:0] in_4,
  input  [2:0] selector,
  output [3:0] \output 
);

  Multiplexer #(.select(3), .width(4)) multiplexer_1 (
    .in0(number_a), .in1(number_b), .in2(in_3), .in3(in_4), .out(\output ), .sel(selector));  // open: in4, in5, in6, in7

  // Notes on the sheet:
  //   number c
  //   number d
  //   4 bit MUX
endmodule
