// Logisim project encoder_.circ as structural Verilog: 1 circuit, main circuit main
module main (
  input  _1,
  input  _2,
  input  _3,
  input  _4,
  input  in_5,
  output out_6,
  output out_7
);

  or or_1 (out_6, _3, in_5);
  or or_2 (out_7, _2, in_5);

  assign _4 = _3;

  // Notes on the sheet:
  //   encoder
endmodule
