// Logisim project 2bit_Alu.circ as structural Verilog: 1 circuit, main circuit main
module main (
  input  B,
  input  A,
  input  Cin,
  input  [1:0] operation,
  input  in_5,
  output result,
  output Cout
);

  wire adder_1_out, and_1_out, multiplexer_1_out, not_1_out, or_1_out;

  not not_1 (not_1_out, B);
  Multiplexer multiplexer_1 (.in0(not_1_out), .in1(B), .out(multiplexer_1_out), .sel(in_5));
  and and_1 (and_1_out, A, multiplexer_1_out);
  or or_1 (or_1_out, A, multiplexer_1_out);
  Adder #(.width(1)) adder_1 (.a(A), .b(multiplexer_1_out), .out(adder_1_out), .cin(Cin), .cout(Cout));
  Multiplexer #(.select(2)) multiplexer_2 (
    .in0(and_1_out), .in1(or_1_out), .in2(adder_1_out), .out(result), .sel(operation));  // open: in3
endmodule
