// Logisim project keyboardd.circ as structural Verilog: 1 circuit, main circuit main
module main (
);

  wire clock_1_out, controlled_buffer_1_out, keyboard_1_avail;
  wire [6:0] keyboard_1_data;

  Clock clock_1 (.out(clock_1_out));
  assign controlled_buffer_1_out = keyboard_1_avail ? clock_1_out : 1'bz;  // Controlled_Buffer controlled_buffer_1
  Keyboard keyboard_1 (
    .clk(controlled_buffer_1_out), .avail(keyboard_1_avail), .data(keyboard_1_data));  // open: re, clr
  TTY tty_1 (.data(keyboard_1_data), .clk(clock_1_out));  // open: we, clr
endmodule
