// Logisim project registerr.circ as structural Verilog: 1 circuit, main circuit main
module main (
  input  [1:0] in_1,
  input  [1:0] in_2,
  input  in_3,
  input  [1:0] in_4,
  input  [3:0] in_5
);

  wire and_1_out, and_2_out, and_3_out, and_4_out, clock_1_out, decoder_1_out0, decoder_1_out1,
       decoder_1_out2, decoder_1_out3;
  wire [3:0] register_1_q, register_2_q, register_3_q, register_4_q;

  Decoder #(.select(2)) decoder_1 (
    .out0(decoder_1_out0), .out1(decoder_1_out1), .out2(decoder_1_out2), .out3(decoder_1_out3), .sel(in_1));  // open: en
  and and_1 (and_1_out, decoder_1_out0, in_3);
  and and_2 (and_2_out, decoder_1_out1, in_3);
  Register #(.width(4)) register_1 (.en(in_5[0]), .Q(register_1_q), .clr(and_1_out));  // open: D, clk
  Register #(.width(4)) register_2 (.en(in_5[0]), .clk(and_2_out), .Q(register_2_q), .clr(clock_1_out));  // open: D
  Clock clock_1 (.out(clock_1_out));
  and and_3 (and_3_out, decoder_1_out2, in_3);
  and and_4 (and_4_out, decoder_1_out3, in_3);
  Register #(.width(4)) register_3 (.en(in_5[0]), .Q(register_3_q), .clr(clock_1_out));  // open: D, clk
  Register #(.width(4)) register_4 (.en(in_5[0]), .clk(and_4_out), .Q(register_4_q), .clr(clock_1_out));  // open: D
  Multiplexer #(.select(2), .width(4)) multiplexer_1 (
    .in0(register_1_q), .in1(register_2_q), .in2(register_3_q), .in3(register_4_q), .sel(in_2));  // open: out
  Multiplexer #(.select(2), .width(4)) multiplexer_2 (
    .in0(register_1_q), .in1(register_2_q), .in2(register_3_q), .in3(register_4_q), .sel(in_4));  // open: out
  // Pins of 1 and 4 bits meet at in_5
endmodule
