// Logisim project lojik_kapilar.circ as structural Verilog: 1 circuit, main circuit main
module main (
  input  in_1,
  input  in_2,
  input  in_3,
  input  in_4,
  input  in_5,
  input  in_6,
  input  in_7,
  input  in_8,
  input  in_9
);

  wire and_1_out, nand_1_out, or_1_out, xor_1_out;

  and and_1 (and_1_out, in_1, in_2);
  or or_1 (or_1_out, in_3, in_4);
  LED led_1 (.in(and_1_out));
  LED led_2 (.in(or_1_out));
  ExactlyOne xor_1 (.out(xor_1_out), .in0(in_5), .in2(in_6), .in4(in_7));
  LED led_3 (.in(xor_1_out));
  nand nand_1 (nand_1_out, in_8, in_9);
  LED led_4 (.in(nand_1_out));
endmodule
