// Logisim project d_flip_flop.circ as structural Verilog: 1 circuit, main circuit main
module main (
  input  in_1,
  input  in_2,
  input  in_3,
  input  in_4
);

  wire d_ff_1_q, d_ff_1_qn;

  D_Flip_Flop d_ff_1 (.clk(in_2), .D(in_4), .Q(d_ff_1_q), .Qn(d_ff_1_qn));  // open: preset, en, reset
endmodule
