// Logisim project t_flip_flop.circ as structural Verilog: 1 circuit, main circuit main
module main (
  input  in_1,
  input  in_2,
  input  in_3,
  input  in_4
);

  wire t_ff_1_q, t_ff_1_qn;

  T_Flip_Flop t_ff_1 (.clk(in_1), .T(in_3), .Q(t_ff_1_q), .Qn(t_ff_1_qn));  // open: preset, reset, en
endmodule
