// Logisim project MUX.circ as structural Verilog
module main (
  input  in_1,
  input  in_2,
  input  in_3,
  input  in_4,
  input  in_5,
  input  in_6,
  output out_7
);

  wire and_1_out, and_2_out, and_3_out, and_4_out, not_1_out, not_2_out, or_1_out;

  not not_1 (not_1_out, in_5);
  not not_2 (not_2_out, in_5);
  and and_1 (and_1_out, in_1, in_5, in_5);
  and and_2 (and_2_out, in_2, not_1_out, in_5);
  and and_3 (and_3_out, in_3, not_2_out, in_5);
  and and_4 (and_4_out, in_4, not_1_out, not_2_out);
  or or_1 (or_1_out, and_1_out, and_2_out, and_3_out, and_4_out);

  assign in_6 = in_5;
endmodule

module HALF_ADDER (
  input  A,
  input  B,
  output out_3,
  output out_4
);

  xor xor_1 (out_3, A, B);
  and and_1 (out_4, A, B);

  // Notes on the sheet:
  //   half adder
endmodule
