// Logisim project tam_cikarici.circ as structural Verilog: 1 circuit, main circuit main
module main (
  input  A,
  input  B,
  input  BIN,
  output diff,
  output bout
);

  wire and_1_out, and_2_out, and_3_out, not_1_out, xor_1_out;

  xor xor_1 (xor_1_out, A, B);
  not not_1 (not_1_out, A);
  xor xor_2 (diff, xor_1_out, BIN);
  and and_1 (and_1_out, not_1_out, B);
  and and_2 (and_2_out, B, BIN);
  and and_3 (and_3_out, not_1_out, BIN);
  or or_1 (bout, and_1_out, and_2_out, and_3_out);

  // Notes on the sheet:
  //   Tam Çıkarıcı
endmodule
